// Logisim project fb-多路选择器型控制器.circ as structural Verilog: 1 circuit, main circuit main
module main (
  input  in_1,
  input  X1,
  input  X2,
  input  in_4
);

  wire clock_1_out, multiplexer_1_out, multiplexer_2_out, not_1_out, not_2_out;
  wire [1:0] d_ff_2_q;

  not not_1 (not_1_out, in_1);
  not not_2 (not_2_out, X2);
  Multiplexer #(.select(2)) multiplexer_1 (
    .in0(1'b0), .in1(X2), .in2(not_1_out), .in3(1'b0), .out(multiplexer_1_out), .sel(d_ff_2_q), .en(in_4));
  Multiplexer #(.select(2)) multiplexer_2 (
    .in0(X1), .in1(not_2_out), .in2(1'b0), .in3(1'b0), .out(multiplexer_2_out), .sel(d_ff_2_q), .en(in_4));
  Clock clock_1 (.out(clock_1_out));
  D_Flip_Flop d_ff_1 (.clk(clock_1_out), .D(multiplexer_1_out), .Q(d_ff_2_q[1]), .en(in_4));  // open: Qn, preset, reset
  D_Flip_Flop d_ff_2 (.clk(clock_1_out), .D(multiplexer_2_out), .Q(d_ff_2_q[0]), .en(in_4));  // open: Qn, preset, reset
endmodule
